// Logisim project lista 5 ex1.circ as structural Verilog: 1 circuit, main circuit main
module main (
  output S
);

  wire A_out, B_out, C_out, not_1_out, or_1_out, or_2_out;

  Button A (.out(A_out));
  Button B (.out(B_out));
  Button C (.out(C_out));
  not not_1 (not_1_out, B_out);
  or or_1 (or_1_out, A_out, B_out);
  or or_2 (or_2_out, not_1_out, C_out);
  and and_1 (S, or_1_out, or_2_out);

  // Notes on the sheet:
  //   Exercício 1
endmodule
