// Logisim project lista 6 adder.circ as structural Verilog: 1 circuit, main circuit main
module main (
  input  cin,
  input  a,
  input  b,
  output cou,
  output s
);

  wire and_1_out, and_2_out, xor_1_out;

  xor xor_1 (xor_1_out, a, b);
  and and_1 (and_1_out, b, a);
  and and_2 (and_2_out, cin, xor_1_out);
  xor xor_2 (s, cin, xor_1_out);
  or or_1 (cou, and_1_out, and_2_out);
endmodule
