// Logisim project lista 6 circuito_arit_4.circ as structural Verilog: 1 circuit, main circuit main
module main (
  input  in_1,
  input  in_2,
  input  in_3,
  input  in_4,
  input  in_5,
  input  in_6,
  input  in_7,
  input  in_8,
  input  in_9,
  output out_10,
  output out_11,
  output out_12,
  output out_13,
  output out_14
);

  wire and_1_out, and_2_out, and_3_out, and_4_out, and_5_out, and_6_out, and_7_out, and_8_out, or_1_out,
       or_2_out, or_3_out, xor_1_out, xor_3_out, xor_6_out, xor_7_out;

  and and_1 (and_1_out, in_6, in_2);
  and and_2 (and_2_out, in_1, xor_1_out);
  xor xor_1 (xor_1_out, in_2, in_6);
  or or_1 (or_1_out, and_1_out, and_2_out);
  xor xor_2 (out_13, in_1, xor_1_out);
  and and_3 (and_3_out, in_7, in_3);
  and and_4 (and_4_out, or_1_out, xor_3_out);
  xor xor_3 (xor_3_out, in_3, in_7);
  or or_2 (or_2_out, and_3_out, and_4_out);
  xor xor_4 (out_14, or_1_out, xor_3_out);
  and and_5 (and_5_out, in_8, in_4);
  and and_6 (and_6_out, or_2_out, xor_6_out);
  xor xor_5 (out_12, or_2_out, xor_6_out);
  xor xor_6 (xor_6_out, in_4, in_8);
  or or_3 (or_3_out, and_5_out, and_6_out);
  and and_7 (and_7_out, in_9, in_5);
  xor xor_7 (xor_7_out, in_5, in_9);
  and and_8 (and_8_out, or_3_out, xor_7_out);
  xor xor_8 (out_11, or_3_out, xor_7_out);
  or or_4 (out_10, and_7_out, and_8_out);

  // Notes on the sheet:
  //   2.
endmodule
