// Logisim project lista 6 circuito_arit_5.circ as structural Verilog: 2 circuits, main circuit main
module main (
  input  carry,
  input  [3:0] in_2,
  input  [3:0] in_3,
  output [4:0] out_4
);

  wire adder_1_cou, adder_2_cou, adder_3_cou;

  adder adder_1 (.cin(carry), .a(in_2[0]), .b(in_3[0]), .cou(adder_1_cou), .s(out_4[0]));
  adder adder_2 (.cin(adder_1_cou), .a(in_2[1]), .b(in_3[1]), .cou(adder_2_cou), .s(out_4[1]));
  adder adder_3 (.cin(adder_2_cou), .a(in_2[2]), .b(in_3[2]), .cou(adder_3_cou), .s(out_4[2]));
  adder adder_4 (.cin(adder_3_cou), .a(in_2[3]), .b(in_3[3]), .cou(out_4[4]), .s(out_4[3]));

  // Notes on the sheet:
  //   3
endmodule

module adder (
  input  cin,
  input  a,
  input  b,
  output cou,
  output s
);

  wire and_1_out, and_2_out, xor_1_out;

  xor xor_1 (xor_1_out, a, b);
  and and_1 (and_1_out, b, a);
  and and_2 (and_2_out, cin, xor_1_out);
  xor xor_2 (s, cin, xor_1_out);
  or or_1 (cou, and_1_out, and_2_out);
endmodule
