// Logisim project lista 6 circuito_arit_7.circ as structural Verilog: 3 circuits, main circuit main
module main (
  input  in_1,
  input  [3:0] in_2,
  input  [3:0] in_3,
  output [3:0] out_4,
  output out_5
);

  Subtractor #(.width(4)) subtractor_1 (.a(in_2), .b(in_3), .out(out_4), .bin(in_1), .bout(out_5));
endmodule

module hs (
  input  a,
  input  b,
  output s,
  output bor
);

  xor xor_1 (s, a, b);
  and and_1 (bor, b, ~a);  // AND_Gate
endmodule

module sub (
  input  bin,
  input  a,
  input  b,
  output sub,
  output bou
);

  wire and_1_out, and_2_out, and_3_out, xor_1_out;

  xor xor_1 (xor_1_out, a, b);
  and and_1 (and_1_out, bin, b);
  and and_2 (and_2_out, bin, ~a);  // AND_Gate
  and and_3 (and_3_out, b, ~a);  // AND_Gate
  ExactlyOne xor_2 (.out(bou), .in0(and_1_out), .in2(and_2_out), .in4(and_3_out));
  xor xor_3 (sub, xor_1_out, bin);
endmodule
