// Logisim project Projeto Sistema.circ as structural Verilog
module main (
);

  wire and_1_out, and_2_out, and_3_out, and_4_out, and_5_out, and_6_out, and_7_out, and_8_out, and_9_out,
       and_10_out, and_11_out, and_12_out, and_13_out, and_14_out, and_15_out, c1_out, c2_out, c3_out,
       c4_out, c5_out, c6_out, c7_out, not_1_out, not_2_out, not_3_out, not_4_out, not_5_out, not_6_out,
       not_7_out, not_8_out, not_9_out, not_10_out, not_11_out, not_12_out, not_13_out, not_14_out, or_1_out,
       or_2_out, or_3_out, or_4_out, or_5_out, or_6_out, or_7_out, or_8_out, or_9_out, or_10_out;

  Button c1 (.out(c1_out));
  Button c2 (.out(c2_out));
  Button c3 (.out(c3_out));
  Button c4 (.out(c4_out));
  Button c5 (.out(c5_out));
  Button c6 (.out(c6_out));
  Button c7 (.out(c7_out));
  or or_1 (or_1_out, c7_out, c6_out, c5_out, c4_out);
  or or_2 (or_2_out, c7_out, c6_out, c3_out, c2_out);
  or or_3 (or_3_out, c7_out, c5_out, c3_out, c1_out);
  and and_1 (and_1_out, or_1_out, or_3_out);
  not not_1 (not_1_out, or_1_out);
  not not_2 (not_2_out, or_2_out);
  not not_3 (not_3_out, or_3_out);
  and and_2 (and_2_out, or_2_out, or_3_out);
  not not_4 (not_4_out, or_1_out);
  not not_5 (not_5_out, or_3_out);
  not not_6 (not_6_out, or_2_out);
  not not_7 (not_7_out, or_1_out);
  not not_8 (not_8_out, or_2_out);
  not not_9 (not_9_out, or_3_out);
  not not_10 (not_10_out, or_2_out);
  not not_11 (not_11_out, or_3_out);
  not not_12 (not_12_out, or_1_out);
  not not_13 (not_13_out, or_2_out);
  not not_14 (not_14_out, or_3_out);
  or or_4 (or_4_out, or_2_out, and_1_out);
  and and_3 (and_3_out, not_1_out, or_2_out);
  and and_4 (and_4_out, or_2_out, or_3_out);
  and and_5 (and_5_out, or_1_out, not_2_out, not_3_out);
  or or_5 (or_5_out, and_2_out, or_1_out);
  and and_6 (and_6_out, not_4_out, or_2_out);
  and and_7 (and_7_out, or_2_out, not_5_out);
  and and_8 (and_8_out, or_1_out, not_6_out, or_3_out);
  and and_9 (and_9_out, not_7_out, not_8_out, or_3_out);
  and and_10 (and_10_out, or_2_out, not_9_out);
  and and_11 (and_11_out, not_10_out, or_3_out);
  and and_12 (and_12_out, or_1_out, not_11_out);
  and and_13 (and_13_out, not_12_out, or_2_out);
  and and_14 (and_14_out, or_1_out, not_13_out);
  and and_15 (and_15_out, or_1_out, not_14_out);
  or or_6 (or_6_out, and_3_out, and_4_out, and_5_out);
  or or_7 (or_7_out, and_6_out, and_7_out, and_8_out);
  or or_8 (or_8_out, and_9_out, and_10_out);
  or or_9 (or_9_out, and_11_out, and_12_out);
  or or_10 (or_10_out, and_13_out, and_14_out, and_15_out);
  _7_Segment_Display u_7_segment_display_1 (
    .g(or_10_out), .f(or_9_out), .a(or_4_out), .b(or_6_out), .e(or_8_out), .d(or_7_out), .c(or_5_out));  // open: dp
endmodule
