// Logisim project lista 5 ex2.circ as structural Verilog: 1 circuit, main circuit main
module main (
);

  wire A_out, and_1_out, and_2_out, B_out, C_out, nand_1_out, not_1_out;

  Button A (.out(A_out));
  Button B (.out(B_out));
  Button C (.out(C_out));
  not not_1 (not_1_out, A_out);
  and and_1 (and_1_out, A_out, C_out);
  nand nand_1 (nand_1_out, B_out, C_out);
  and and_2 (and_2_out, not_1_out, B_out, C_out);
  // OR_Gate or_1 has open pins: in0=and_1_out, in2=nand_1_out, in4=and_2_out, out=open

  // Notes on the sheet:
  //   Exercício 2
endmodule
