// Logisim project lista 5 ex5.circ as structural Verilog: 1 circuit, main circuit main
// x1
module main (
  output x1
);

  wire and_1_out, and_2_out, not_1_out, not_2_out, x1_2_out, x1_out;

  Button u_x1 (.out(x1_out));
  Button x1_2 (.out(x1_2_out));
  not not_1 (not_1_out, x1_out);
  not not_2 (not_2_out, x1_2_out);
  and and_1 (and_1_out, not_1_out, x1_2_out);
  and and_2 (and_2_out, x1_out, x1_out, not_2_out);
  or or_1 (x1, and_1_out, and_2_out);

  // Notes on the sheet:
  //   Exercício 5
  //   Funciona da mesma forma que a porta XOR porém com 2 entradas.
endmodule
