// Logisim project lista 5.circ as structural Verilog: 1 circuit, main circuit main
module main (
  output S
);

  wire A_2_out, A_out, and_1_out, and_2_out, B_2_out, B_out, C_2_out, C_out, nand_1_out, not_1_out,
       not_2_out, or_1_out, or_2_out;

  Button A (.out(A_out));
  Button B (.out(B_out));
  not not_1 (not_1_out, B_out);
  Button C (.out(C_out));
  Button A_2 (.out(A_2_out));
  not not_2 (not_2_out, A_2_out);
  Button B_2 (.out(B_2_out));
  Button C_2 (.out(C_2_out));
  or or_1 (or_1_out, A_out, B_out);
  or or_2 (or_2_out, not_1_out, C_out);
  and and_1 (and_1_out, A_2_out, C_2_out);
  nand nand_1 (nand_1_out, B_2_out, C_2_out);
  and and_2 (and_2_out, not_2_out, B_2_out, C_2_out);
  and and_3 (S, or_1_out, or_2_out);
  // OR_Gate or_3 has open pins: in0=and_1_out, in2=nand_1_out, in4=and_2_out, out=open

  // Notes on the sheet:
  //   Exercício 1
  //   Exercício 2
  //   Exercício 3
endmodule
