// Logisim project lista 6 circuito_arit_3.circ as structural Verilog: 1 circuit, main circuit main
module main (
  input  in_1,
  input  in_2,
  input  in_3,
  input  in_4,
  input  in_5,
  output out_6,
  output out_7,
  output out_8,
  output out_9
);

  wire and_2_out, and_3_out, xor_2_out;

  and and_1 (out_6, in_2, in_1);
  xor xor_1 (out_7, in_1, in_2);
  xor xor_2 (xor_2_out, in_4, in_5);
  and and_2 (and_2_out, in_5, in_4);
  and and_3 (and_3_out, in_3, xor_2_out);
  xor xor_3 (out_9, in_3, xor_2_out);
  or or_1 (out_8, and_2_out, and_3_out);

  // Notes on the sheet:
  //   1.
endmodule
