// Logisim project lista 6 circuito_arit_6.circ as structural Verilog: 3 circuits, main circuit main
module main (
  input  in_1,
  input  [7:0] in_2,
  input  [7:0] in_3,
  output [7:0] out_4,
  output out_5
);

  wire adder2_1_carry_2;

  adder2 adder2_1 (.a(in_2[3:0]), .b(in_3[3:0]), .carry(in_1), .s(out_4[3:0]), .carry_2(adder2_1_carry_2));
  adder2 adder2_2 (.a(in_2[7:4]), .b(in_3[7:4]), .carry(adder2_1_carry_2), .s(out_4[7:4]), .carry_2(out_5));

  // Notes on the sheet:
  //   4
endmodule

module adder2 (
  input  carry,
  input  [3:0] a,
  input  [3:0] b,
  output [3:0] s,
  output carry_2
);

  wire adder_1_cou, adder_2_cou, adder_3_cou;

  adder adder_1 (.cin(carry), .a(a[0]), .b(b[0]), .cou(adder_1_cou), .s(s[0]));
  adder adder_2 (.cin(adder_1_cou), .a(a[1]), .b(b[1]), .cou(adder_2_cou), .s(s[1]));
  adder adder_3 (.cin(adder_2_cou), .a(a[2]), .b(b[2]), .cou(adder_3_cou), .s(s[2]));
  adder adder_4 (.cin(adder_3_cou), .a(a[3]), .b(b[3]), .cou(carry_2), .s(s[3]));
endmodule

module adder (
  input  cin,
  input  a,
  input  b,
  output cou,
  output s
);

  wire and_1_out, and_2_out, xor_1_out;

  xor xor_1 (xor_1_out, a, b);
  and and_1 (and_1_out, b, a);
  and and_2 (and_2_out, cin, xor_1_out);
  xor xor_2 (s, cin, xor_1_out);
  or or_1 (cou, and_1_out, and_2_out);
endmodule
