// Logisim project lista 6 circuito_arit_8.circ as structural Verilog: 1 circuit, main circuit main
module main (
  input  [3:0] in_1,
  output [3:0] out_2
);

  Negator #(.width(4)) negator_1 (.in(in_1), .out(out_2));
endmodule
