// Logisim project lista 6 circuito_arit_9.circ as structural Verilog: 1 circuit, main circuit main
module main (
  input  in_1,
  input  [3:0] in_2,
  input  [3:0] in_3,
  output [3:0] out_4,
  output out_5
);

  wire [3:0] negator_1_out;

  Adder #(.width(4)) adder_1 (.a(in_2), .b(negator_1_out), .out(out_4), .cin(in_1), .cout(out_5));
  Negator #(.width(4)) negator_1 (.in(in_3), .out(negator_1_out));
endmodule
