// Logisim project lista 7 decod_1.circ as structural Verilog: 1 circuit, main circuit main
module main (
  input  in_1,
  input  in_2,
  output out_3,
  output out_4,
  output out_5,
  output out_6
);

  and and_1 (out_3, ~in_2, ~in_1);  // AND_Gate
  and and_2 (out_4, in_2, ~in_1);  // AND_Gate
  and and_3 (out_5, ~in_2, in_1);  // AND_Gate
  and and_4 (out_6, in_2, in_1);
endmodule
