// Logisim project lista 7 decod_2.circ as structural Verilog: 1 circuit, main circuit main
module main (
  input  in_1,
  input  in_2,
  input  in_3,
  output out_4,
  output out_5,
  output out_6,
  output out_7,
  output out_8,
  output out_9,
  output out_10,
  output out_11
);

  and and_1 (out_4, ~in_3, ~in_1, ~in_2);  // AND_Gate
  and and_2 (out_5, in_3, ~in_1, ~in_2);  // AND_Gate
  and and_3 (out_6, in_3, in_1, ~in_2);  // AND_Gate
  and and_4 (out_7, ~in_3, ~in_1, in_2);  // AND_Gate
  and and_5 (out_8, ~in_3, in_1, in_2);  // AND_Gate
  and and_6 (out_9, ~in_3, in_1, ~in_2);  // AND_Gate
  and and_7 (out_10, in_3, ~in_1, in_2);  // AND_Gate
  and and_8 (out_11, in_3, in_2, in_1);
endmodule
