// Logisim project lista 7 memoria_sim.circ as structural Verilog: 1 circuit, main circuit main
module main (
  input  [7:0] in_1,
  input  [3:0] in_2,
  input  in_3,
  input  in_4,
  input  in_5,
  output [7:0] out_6
);

  wire not_1_out;

  assign out_6 = in_4 ? in_1 : 8'bz;  // Controlled_Buffer controlled_buffer_1
  not not_1 (not_1_out, in_4);
  RAM #(.addrWidth(4)) ram_1 (.addr(in_2), .data(out_6), .clk(in_5), .ld(not_1_out), .clr(in_3));  // open: sel
endmodule
