// Logisim project relogio.circ as structural Verilog: 3 circuits, main circuit Relógio
module \Relógio  (
  output [3:0] out_1,
  output [3:0] out_2,
  output [3:0] out_3,
  output [3:0] out_4,
  output [3:0] out_5,
  output [3:0] out_6
);

  wire and_1_out, clock_1_out, counter_2_carry, counter_3_carry, counter_4_carry, counter_5_carry,
       counter_6_carry, dezh_1_out_5, unidh_1_out_5;

  dezH dezh_1 (.in_1(out_4[0]), .in_2(out_4[1]), .in_3(out_4[2]), .in_4(out_4[3]), .out_5(dezh_1_out_5));
  unidH unidh_1 (.in_1(out_1[0]), .in_2(out_1[1]), .in_3(out_1[2]), .in_4(out_1[3]), .out_5(unidh_1_out_5));
  and and_1 (and_1_out, dezh_1_out_5, unidh_1_out_5);
  Hex_Digit_Display hex_digit_display_1 (.value(out_4));  // open: dp
  Counter #(.width(4), .max('h2), .trigger("falling")) counter_1 (
    .Q(out_4), .clk(counter_2_carry), .clr(and_1_out));  // open: load, D, count, carry
  Hex_Digit_Display hex_digit_display_2 (.value(out_1));  // open: dp
  Counter #(.width(4), .max('h9), .trigger("falling")) counter_2 (
    .Q(out_1), .carry(counter_2_carry), .clk(counter_3_carry), .clr(and_1_out));  // open: load, D, count
  Hex_Digit_Display hex_digit_display_3 (.value(out_6));  // open: dp
  Counter #(.width(4), .max('h5), .trigger("falling")) counter_3 (
    .Q(out_6), .carry(counter_3_carry), .clk(counter_4_carry), .clr(and_1_out));  // open: load, D, count
  Hex_Digit_Display hex_digit_display_4 (.value(out_2));  // open: dp
  Counter #(.width(4), .max('h9), .trigger("falling")) counter_4 (
    .Q(out_2), .carry(counter_4_carry), .clk(counter_5_carry), .clr(and_1_out));  // open: load, D, count
  Hex_Digit_Display hex_digit_display_5 (.value(out_5));  // open: dp
  Counter #(.width(4), .max('h5), .trigger("falling")) counter_5 (
    .Q(out_5), .carry(counter_5_carry), .clk(counter_6_carry), .clr(and_1_out));  // open: load, D, count
  Hex_Digit_Display hex_digit_display_6 (.value(out_3));  // open: dp
  Counter #(.width(4), .max('h9), .trigger("falling")) counter_6 (
    .Q(out_3), .carry(counter_6_carry), .clk(clock_1_out), .clr(and_1_out));  // open: load, D, count
  Clock clock_1 (.out(clock_1_out));
endmodule

module unidH (
  input  in_1,
  input  in_2,
  input  in_3,
  input  in_4,
  output out_5
);

  wire not_1_out, not_2_out, not_3_out;

  not not_1 (not_1_out, in_1);
  not not_2 (not_2_out, in_2);
  not not_3 (not_3_out, in_4);
  and and_1 (out_5, not_1_out, not_2_out, in_3, not_3_out);
endmodule

module dezH (
  input  in_1,
  input  in_2,
  input  in_3,
  input  in_4,
  output out_5
);

  wire not_1_out, not_2_out, not_3_out;

  not not_1 (not_1_out, in_1);
  not not_2 (not_2_out, in_3);
  not not_3 (not_3_out, in_4);
  unidH unidh_1 ();  // open: in_1, in_2, in_3, in_4, out_5
  and and_1 (out_5, not_1_out, in_2, not_2_out, not_3_out);
endmodule
